# Fritzing sketch schematic (saved by Fritzing 0.9.3b)
perfboards: 1

parts:
  Part1 = Arduino Mega 2560 (Rev3)
  ZS-042_RTC1 = ZS-042 RTC Module
  U1 = 2-Channel 5v Relay Shield [package=relay-2ch5v10a]
  U2 = 2-Channel 5v Relay Shield [package=relay-2ch5v10a]
  M1 = DC Motor
  S1 = Toggle Switch [package=THT]

nets:
  N1: Part1.D19/RX1, ZS-042_RTC1.GND
  N2: Part1.D18/TX1, ZS-042_RTC1.VCC
  N3: Part1.D17_PWM/RX2, ZS-042_RTC1.SDA
  N4: Part1.D16_PWM/TX2, ZS-042_RTC1.SCL
  N5: Part1.D15/RX3, ZS-042_RTC1.SQW
  N6: Part1.D14/TX3, ZS-042_RTC1.32K
  VCC: Part1.5V, U1.VCC, U2.VCC
  N7: Part1.D25, S1.L1
  N8: Part1.D27, U2.IN1
  N9: Part1.D29, U2.IN2
  N10: Part1.D31, U1.IN1
  GND: Part1.GND, U2.GND
  N11: U2.K1-In, M1.pin_1
  N12: U2.K2-In, M1.pin_2

custom parts:
  2-Channel 5v Relay Shield: 2 Channel 5v Relay Shield w. 2x SPD-06VDC-SD-C
